// Digital circuit accum.dig as structural Verilog
module accum (
  input  A3,
  input  B3,
  input  A2,
  input  B2,
  input  A1,
  input  B2_2,
  input  A0,
  input  B0,
  input  cin,
  input  A7,
  input  B7,
  input  A6,
  input  B6,
  input  A5,
  input  B6_2,
  input  A4,
  input  B4,
  input  cin_2,
  input  B13,
  input  B12,
  input  B12_2,
  input  B10,
  input  INC_DEC,
  input  CLK,
  input  A11,
  input  B17,
  input  A10,
  input  B16,
  input  A9,
  input  B16_2,
  input  A8,
  input  B14,
  input  ADD_SUB,
  input  EN,
  input  DIR,
  input  clk_2
);

  wire add_1_s, add_2_c_o, add_2_s, add_3_c_o, add_3_s, add_4_c_o, add_4_s, add_5_s, add_6_c_o, add_6_s,
       add_7_c_o, add_7_s, add_8_c_o, add_8_s, add_9_s, add_10_c_o, add_10_s, add_11_c_o, add_11_s,
       add_12_c_o, add_12_s, add_13_s, add_14_c_o, add_14_s, add_15_c_o, add_15_s, add_16_c_o, add_16_s,
       and_1_out, and_2_out, d_ff_1_q, d_ff_2_q, d_ff_3_q, d_ff_4_q, d_ff_5_q, d_ff_6_nq, d_ff_6_q,
       not_1_out, not_2_out, not_3_out, not_4_out, not_5_out, not_6_out, or_1_out, xor_1_out, xor_2_out,
       xor_3_out, xor_4_out, xor_5_out, xor_6_out, xor_7_out, xor_8_out, xor_9_out, xor_10_out, xor_11_out;

  Add add_1 (.a(A3), .b(B3), .c_i(add_2_c_o), .s(add_1_s));  // open: c_o
  Add add_2 (.a(A2), .b(B2), .c_i(add_3_c_o), .s(add_2_s), .c_o(add_2_c_o));
  Add add_3 (.a(A1), .b(B2_2), .c_i(add_4_c_o), .s(add_3_s), .c_o(add_3_c_o));
  Add add_4 (.a(A0), .b(B0), .c_i(cin), .s(add_4_s), .c_o(add_4_c_o));
  LED led_1 (.in(add_1_s));
  LED led_2 (.in(add_2_s));
  LED led_3 (.in(add_3_s));
  LED led_4 (.in(add_4_s));
  xor xor_1 (xor_1_out, B13, INC_DEC);
  xor xor_2 (xor_2_out, B12, INC_DEC);
  xor xor_3 (xor_3_out, B12_2, INC_DEC);
  xor xor_4 (xor_4_out, B10, INC_DEC);
  not not_1 (not_1_out, B7);
  not not_2 (not_2_out, B6);
  not not_3 (not_3_out, B6_2);
  not not_4 (not_4_out, B4);
  Add add_5 (.a(A7), .b(not_1_out), .c_i(add_6_c_o), .s(add_5_s));  // open: c_o
  Add add_6 (.a(A6), .b(not_2_out), .c_i(add_7_c_o), .s(add_6_s), .c_o(add_6_c_o));
  Add add_7 (.a(A5), .b(not_3_out), .c_i(add_8_c_o), .s(add_7_s), .c_o(add_7_c_o));
  Add add_8 (.a(A4), .b(not_4_out), .c_i(cin_2), .s(add_8_s), .c_o(add_8_c_o));
  Add add_9 (.a(d_ff_1_q), .b(xor_1_out), .c_i(add_10_c_o), .s(add_9_s));  // open: c_o
  Add add_10 (.a(d_ff_2_q), .b(xor_2_out), .c_i(add_11_c_o), .s(add_10_s), .c_o(add_10_c_o));
  Add add_11 (.a(d_ff_3_q), .b(xor_3_out), .c_i(add_12_c_o), .s(add_11_s), .c_o(add_11_c_o));
  Add add_12 (.a(d_ff_4_q), .b(xor_4_out), .c_i(INC_DEC), .s(add_12_s), .c_o(add_12_c_o));
  LED led_5 (.in(add_5_s));
  LED led_6 (.in(add_6_s));
  LED led_7 (.in(add_7_s));
  LED led_8 (.in(add_8_s));
  D_FF d_ff_1 (.D(add_9_s), .C(CLK), .Q(d_ff_1_q));  // open: nQ
  LED led_9 (.in(add_9_s));
  D_FF d_ff_2 (.D(add_10_s), .C(CLK), .Q(d_ff_2_q));  // open: nQ
  LED led_10 (.in(add_10_s));
  D_FF d_ff_3 (.D(add_11_s), .C(CLK), .Q(d_ff_3_q));  // open: nQ
  LED led_11 (.in(add_11_s));
  D_FF d_ff_4 (.D(add_12_s), .C(CLK), .Q(d_ff_4_q));  // open: nQ
  LED led_12 (.in(add_12_s));
  not not_5 (not_5_out, EN);
  LED O3 (.in(d_ff_1_q));
  LED O2 (.in(d_ff_2_q));
  LED O1 (.in(d_ff_3_q));
  LED O0 (.in(d_ff_4_q));
  xor xor_5 (xor_5_out, B17, ADD_SUB);
  xor xor_6 (xor_6_out, B16, ADD_SUB);
  xor xor_7 (xor_7_out, B16_2, ADD_SUB);
  xor xor_8 (xor_8_out, B14, ADD_SUB);
  xor xor_9 (xor_9_out, d_ff_5_q, EN);
  xor xor_10 (xor_10_out, d_ff_5_q, DIR, d_ff_6_q);
  and and_1 (and_1_out, d_ff_6_q, not_5_out);
  Add add_13 (.a(A11), .b(xor_5_out), .c_i(add_14_c_o), .s(add_13_s));  // open: c_o
  Add add_14 (.a(A10), .b(xor_6_out), .c_i(add_15_c_o), .s(add_14_s), .c_o(add_14_c_o));
  Add add_15 (.a(A9), .b(xor_7_out), .c_i(add_16_c_o), .s(add_15_s), .c_o(add_15_c_o));
  Add add_16 (.a(A8), .b(xor_8_out), .c_i(ADD_SUB), .s(add_16_s), .c_o(add_16_c_o));
  and and_2 (and_2_out, EN, xor_10_out);
  or or_1 (or_1_out, and_2_out, and_1_out);
  LED led_13 (.in(add_13_s));
  LED led_14 (.in(add_14_s));
  LED led_15 (.in(add_15_s));
  LED led_16 (.in(add_16_s));
  LED Q0 (.in(xor_9_out));
  LED Q1 (.in(or_1_out));
  D_FF d_ff_5 (.D(xor_9_out), .C(clk_2), .Q(d_ff_5_q));  // open: nQ
  D_FF d_ff_6 (.D(or_1_out), .C(clk_2), .Q(d_ff_6_q), .nQ(d_ff_6_nq));
  LED Q0_2 (.in(d_ff_5_q));
  LED Q1_2 (.in(d_ff_6_q));
  xor xor_11 (xor_11_out, d_ff_5_q, d_ff_6_q);
  not not_6 (not_6_out, xor_11_out);
  LED A (.in(d_ff_6_nq));
  LED B (.in(d_ff_6_q));
  LED D (.in(xor_11_out));
  LED C (.in(not_6_out));
endmodule
